# Fritzing sketch V1_NW_MySensors (saved by Fritzing 0.9.3b)
stripboards: 1

parts:
  HLK-PM1 = HLK-PM01
  Onderdeel1 = Arduino Pro Mini (3.3V)
  Onderdeel2 = Adafruit 4-channel I2C-safe Bi-directional Logic Level Converter [part_number="Adafruit #757"]
  Q1 = DC-DC Step Down LM2596S [package=breakout]
  J1 = female pin header, 2 pins [form="♀ (female)"]
  J2 = female pin header, 2 pins [form="♀ (female)"]  # not connected
  J3 = female pin header, 2 pins [form="♀ (female)"]
  R = Resistor [tolerance=±5% resistance=10k package="0603 [SMD]"]
  U1 = RF-LINK_RX [package=rf-link_rx]
  Part1 = Arduino Leonardo (Rev3b)  # not connected

nets:
  N1: HLK-PM1.+Vo, U1.+5V
  N2: Onderdeel1.DTR, Onderdeel2.B1
  N3: Onderdeel1.TXO, J3.pin1
  N4: Onderdeel1.RXI, Onderdeel2.B2
  GND: Onderdeel1.GND, Onderdeel2.GND, J1.pin1, J1.pin2, U1.GND
  N5: Onderdeel1.VCC, Onderdeel2.LV, R.Pin_0
  N6: Onderdeel1.D3, Onderdeel2.A3
  N7: Onderdeel2.B3, U1.DATA
  N8: Q1.OUT-, R.Pin_1

custom parts:
  Adafruit 4-channel I2C-safe Bi-directional Logic Level Converter: Because the Arduino (and Basic Stamp) are 5V devices, and most modern sensors, displays, flash cards and modes are 3.3V-only, many makers find that they need to perform level shifting/conversion to protect the 3.3V device from 5V. We do have some other handy level shifters in the shop, from the DIP 74LVC245 to the fancy bi-directional TXB0108. However, neither of these are happy to work with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
