# Fritzing sketch V1_NW_MySensors_RPi (saved by Fritzing 0.9.3b)

parts:
  Raspberry_Pi1 = Raspberry Pi 2
  RFM1 = RFM69HCW ISM Transciever
  U1 = RF-LINK_RX [package=rf-link_rx]
  U2 = attiny85 [package=dip]
  R1 = Resistor [tolerance=±5% resistance=1k package="0603 [SMD]"]
  R2 = 1000 Ω Resistor [package="0603 [SMD]"]
  R3 = 1000 Ω Resistor [package="0603 [SMD]"]
  U3 = RF-LINK_TX [package=rf-link_tx]
  Part1 = BH1750
  U4 = MLX90614 [package=to-39]  # not connected
  Sensore_PIR_HC-SR502 = HC-SR501 Body Sensor Module

nets:
  3V3: Raspberry_Pi1.3v3, Raspberry_Pi1.3V3, RFM1.13_3.3V, Part1.VCC
  N1: Raspberry_Pi1.GPIO2, Part1.SDA
  N2: Raspberry_Pi1.GPIO3, Part1.SCL
  N3: Raspberry_Pi1.GIPO4, Sensore_PIR_HC-SR502.OUT
  GND: Raspberry_Pi1.GND, RFM1.1_GND, U1.GND, U2.Pin_4, U3.GND, Part1.GND, Sensore_PIR_HC-SR502.GND
  N4: Raspberry_Pi1.GIPO17, U3.DATA
  N5: Raspberry_Pi1.GIPO10, RFM1.3_MOSI
  N6: Raspberry_Pi1.GIPO9, RFM1.2_MISO
  N7: Raspberry_Pi1.GIPO11, RFM1.4_SCK
  N8: Raspberry_Pi1.GIPO8, RFM1.5_NSS_(CS)
  N9: Raspberry_Pi1.GIPO25, RFM1.14_DIO0
  N10: Raspberry_Pi1.GIPO18, R2.Pin_0
  +5V: Raspberry_Pi1.5V, U1.+5V, U2.Pin_8, U3.+5V, Sensore_PIR_HC-SR502.VCC
  N11: U1.DATA, R3.Pin_0
  N12: U2.Pin_1, R1.Pin_1
  N13: U2.Pin_2, R2.Pin_1
  N14: U2.Pin_3, R3.Pin_1

custom parts:
  RFM69HCW ISM Transciever: RF Transceiver by Hope RF. Well supported Arduino libraries are available. This ISM band transceiver is available in several frequencies e.g. 433MHz and 915MHz and it is also available in various feature versions.
  1000 Ω Resistor: A generic resistor (0.25W)
  BH1750: Light Sensor
  HC-SR501 Body Sensor Module: Pyroelectric Infrared PIR Motion Sensor Detector Module
